# Fritzing sketch wiring_diagram (saved by Fritzing 1.0.0rc)
breadboards: 1

parts:
  Mod1 = Amica NodeMCU DEVKIT 1.0
  Mod2 = SDS011 - dust sensor [part_number=1]

nets:
  N1: Mod1.pin2, Mod1.pin_29, Mod2.GND
  N2: Mod1.pin7, Mod2.RXD
  N3: Mod1.pin8, Mod2.TXD
  N4: Mod1.pin_30, Mod2.5V

custom parts:
  SDS011 - dust sensor: The SDS 011 Sensor is a quite recent Air Quality Sensor developed by inovafit, a spin-off from the university of Jinan (in Shandong). With its size, it is probably one of the best sensor in terms of accuracy: While other sensors tend to focus on shrinking the sensor size, the SDS 011 has opted for a size tradeoff allowing it to use a larger fan. And the larger the fan, the better the quality.
