# Fritzing sketch esp32_display_wiring_diagram (saved by Fritzing 1.0.0rc)
breadboards: 1

parts:
  OLED_I2C1 = OLED 128x64 I2C Monochrome Display
  U1 = LuaNode32 / ESP32 [part_number=ESP32S-PIN30]

nets:
  N1: OLED_I2C1.SDA, U1.D21
  N2: OLED_I2C1.SCK, U1.D22
  VDD: OLED_I2C1.VDD, U1.3V3
  GND: OLED_I2C1.GND, U1.GND

custom parts:
  LuaNode32 / ESP32: New Image for LuaNode32 DOIT ESP32 DEVKIT V1. Base parts from LuaNode32 / ESP32 ESP32 based LuaNode32 by G.Noorlander DOIT Esp32 DevKit v1 (30 pins long, 11 pins width) by Werner Rothschopf (modified by vanepp Dec 2018)
