# Fritzing sketch esp32_sds011_wiring_diagram (saved by Fritzing 1.0.0rc)

parts:
  Mod2 = SDS011 - dust sensor [part_number=1]
  U1 = LuaNode32 / ESP32 [part_number=ESP32S-PIN30]

nets:
  5V: Mod2.5V, U1.Vin
  GND: Mod2.GND, U1.GND
  N1: Mod2.RXD, U1.TX2
  N2: Mod2.TXD, U1.RX2

custom parts:
  SDS011 - dust sensor: The SDS 011 Sensor is a quite recent Air Quality Sensor developed by inovafit, a spin-off from the university of Jinan (in Shandong). With its size, it is probably one of the best sensor in terms of accuracy: While other sensors tend to focus on shrinking the sensor size, the SDS 011 has opted for a size tradeoff allowing it to use a larger fan. And the larger the fan, the better the quality.
  LuaNode32 / ESP32: New Image for LuaNode32 DOIT ESP32 DEVKIT V1. Base parts from LuaNode32 / ESP32 ESP32 based LuaNode32 by G.Noorlander DOIT Esp32 DevKit v1 (30 pins long, 11 pins width) by Werner Rothschopf (modified by vanepp Dec 2018)
