# Fritzing sketch esp32_wiring_diagram (saved by Fritzing 1.0.0rc)
breadboards: 1

parts:
  Mod2 = SDS011 - dust sensor [part_number=1]
  OLED_I2C1 = OLED 128x64 I2C Monochrome Display
  U1 = LuaNode32 / ESP32 [part_number=ESP32S-PIN30]
  R1 = Resistor [tolerance=±5% power=0.25W resistance=220 package=THT]
  LED1 = LEDs [package=led10mm]
  Raspberry_Pi_1 = Raspberry Pi 3 [part_number=RPI-3-V1.2]  # not connected

nets:
  5V: Mod2.5V, U1.Vin
  GND: Mod2.GND, OLED_I2C1.GND, U1.GND, LED1.A
  N1: Mod2.RXD, U1.TX2
  N2: Mod2.TXD, U1.RX2
  N3: OLED_I2C1.SDA, U1.D21
  N4: OLED_I2C1.SCK, U1.D22
  VDD: OLED_I2C1.VDD, U1.3V3
  N5: U1.D4, R1.Pin_1
  N6: R1.Pin_0, LED1.C

custom parts:
  SDS011 - dust sensor: The SDS 011 Sensor is a quite recent Air Quality Sensor developed by inovafit, a spin-off from the university of Jinan (in Shandong). With its size, it is probably one of the best sensor in terms of accuracy: While other sensors tend to focus on shrinking the sensor size, the SDS 011 has opted for a size tradeoff allowing it to use a larger fan. And the larger the fan, the better the quality.
  LuaNode32 / ESP32: New Image for LuaNode32 DOIT ESP32 DEVKIT V1. Base parts from LuaNode32 / ESP32 ESP32 based LuaNode32 by G.Noorlander DOIT Esp32 DevKit v1 (30 pins long, 11 pins width) by Werner Rothschopf (modified by vanepp Dec 2018)
