# Fritzing sketch esp8266_display_wiring_diagram (saved by Fritzing 1.0.0rc)
breadboards: 1

parts:
  Mod1 = Amica NodeMCU DEVKIT 1.0
  OLED_I2C1 = OLED 128x64 I2C Monochrome Display

nets:
  N1: Mod1.pin1, OLED_I2C1.VDD
  N2: Mod1.pin2, OLED_I2C1.GND
  N3: Mod1.pin_13, OLED_I2C1.SDA
  N4: Mod1.pin_14, OLED_I2C1.SCK
