# Fritzing sketch esp8266_wiring_diagram (saved by Fritzing 1.0.0rc)
breadboards: 1

parts:
  Mod1 = Amica NodeMCU DEVKIT 1.0
  Mod2 = SDS011 - dust sensor [part_number=1]
  OLED_I2C1 = OLED 128x64 I2C Monochrome Display

nets:
  N1: Mod1.pin1, OLED_I2C1.VDD
  GND: Mod1.pin2, Mod1.pin_29, Mod2.GND, OLED_I2C1.GND
  N2: Mod1.pin7, Mod2.RXD
  N3: Mod1.pin8, Mod2.TXD
  N4: Mod1.pin_13, OLED_I2C1.SDA
  N5: Mod1.pin_14, OLED_I2C1.SCK
  N6: Mod1.pin_30, Mod2.5V

custom parts:
  SDS011 - dust sensor: The SDS 011 Sensor is a quite recent Air Quality Sensor developed by inovafit, a spin-off from the university of Jinan (in Shandong). With its size, it is probably one of the best sensor in terms of accuracy: While other sensors tend to focus on shrinking the sensor size, the SDS 011 has opted for a size tradeoff allowing it to use a larger fan. And the larger the fan, the better the quality.
